// Logisim project Calcrator.circ as structural Verilog: 7 circuits, main circuit main
module main (
);

  wire clock_1_out, mch64_1_memory_write, mch64_1_true, RESET_out;
  wire [7:0] mch64_1_instruction_out;
  wire [15:0] PROGRAM_data;
  wire [63:0] mch64_1_memory_address, mch64_1_memory_write_data, MEMORY_dout;

  Clock clock_1 (.out(clock_1_out));
  Button RESET (.out(RESET_out));
  mch64 mch64_1 (
    .CLOCK(clock_1_out), .RESET(RESET_out), .INSTRUCTION_DATA(PROGRAM_data), .MEMORY_READ_DATA(MEMORY_dout),
    .INSTRUCTION_OUT(mch64_1_instruction_out), .MEMORY_ADDRESS(mch64_1_memory_address),
    .MEMORY_WRITE_DATA(mch64_1_memory_write_data), .MEMORY_WRITE(mch64_1_memory_write), .TRUE(mch64_1_true));
  ROM #(.dataWidth(16)) PROGRAM (.addr(mch64_1_instruction_out), .data(PROGRAM_data));
  RAM #(.asyncread("true"), .dataWidth(64)) MEMORY (
    .addr(mch64_1_memory_address[7:0]), .we(mch64_1_memory_write), .oe(mch64_1_true), .clk(clock_1_out),
    .din(mch64_1_memory_write_data), .dout(MEMORY_dout));

  // Notes on the sheet:
  //   contents of PROGRAM (hex, n*v repeats v):
  //   5205 5407 1650 5803 3ae0 5c0a 7170 6f80
endmodule

module ALU (
  input  [63:0] IN0,
  input  [63:0] IN1,
  input  [1:0] MODE,
  output [63:0] RESULT,
  output ZERO,
  output NEGATIVE,
  output CARRY
);

  wire adder_1_cout, subtractor_1_bout;
  wire [63:0] adder_1_out, divider_1_out, multiplier_1_out, subtractor_1_out;

  Adder #(.width(64)) adder_1 (.a(IN0), .b(IN1), .out(adder_1_out), .cout(adder_1_cout));  // open: cin
  Subtractor #(.width(64)) subtractor_1 (
    .a(IN0), .b(IN1), .out(subtractor_1_out), .bout(subtractor_1_bout));  // open: bin
  Multiplier #(.width(64)) multiplier_1 (.a(IN0), .b(IN1), .out(multiplier_1_out));  // open: cin, cout
  Divider #(.width(64)) divider_1 (.a(IN0), .b(IN1), .out(divider_1_out));  // open: upper, rem
  Multiplexer #(.select(2), .width(64)) multiplexer_1 (
    .in0(adder_1_out), .in1(subtractor_1_out), .in2(multiplier_1_out), .in3(divider_1_out),
    .out({NEGATIVE, RESULT[62:0]}), .sel(MODE));
  Multiplexer #(.select(2)) multiplexer_2 (
    .in0(adder_1_cout), .in1(subtractor_1_bout), .in2(1'b0), .in3(1'b0), .out(CARRY), .sel(MODE));
  Comparator #(.width(64)) comparator_1 (.a({NEGATIVE, RESULT[62:0]}), .b({64{1'b0}}), .eq(ZERO));  // open: gt, lt

  assign RESULT[63] = NEGATIVE;
endmodule

module regist (
  input  [63:0] DATA_IN,
  input  [2:0] READ_A_SELECT,
  input  [2:0] READ_B_SELECT,
  input  [2:0] WRITE_SELECT,
  input  WRITE,
  input  CLOCK,
  input  RESET,
  output [63:0] DATA_A_OUT,
  output [63:0] DATA_B_OUT
);

  wire demultiplexer_2_out0, demultiplexer_2_out1, demultiplexer_2_out2, demultiplexer_2_out3,
       demultiplexer_2_out4, demultiplexer_2_out5, demultiplexer_2_out6, demultiplexer_2_out7;
  wire [63:0] demultiplexer_1_out0, demultiplexer_1_out1, demultiplexer_1_out2, demultiplexer_1_out3,
       demultiplexer_1_out4, demultiplexer_1_out5, demultiplexer_1_out6, demultiplexer_1_out7, R0_q, R1_q,
       R2_q, R3_q, R4_q, R5_q, R6_q, R7_q;

  Demultiplexer #(.select(3), .width(64)) demultiplexer_1 (
    .out0(demultiplexer_1_out0), .out1(demultiplexer_1_out1), .out2(demultiplexer_1_out2),
    .out3(demultiplexer_1_out3), .out4(demultiplexer_1_out4), .out5(demultiplexer_1_out5),
    .out6(demultiplexer_1_out6), .out7(demultiplexer_1_out7), .in(DATA_IN), .sel(WRITE_SELECT));
  Demultiplexer #(.select(3)) demultiplexer_2 (
    .out0(demultiplexer_2_out0), .out1(demultiplexer_2_out1), .out2(demultiplexer_2_out2),
    .out3(demultiplexer_2_out3), .out4(demultiplexer_2_out4), .out5(demultiplexer_2_out5),
    .out6(demultiplexer_2_out6), .out7(demultiplexer_2_out7), .in(WRITE), .sel(WRITE_SELECT));
  Register #(.width(64)) R0 (.D(demultiplexer_1_out0), .en(demultiplexer_2_out0), .clk(CLOCK), .Q(R0_q), .clr(RESET));
  Register #(.width(64)) R1 (.D(demultiplexer_1_out1), .en(demultiplexer_2_out1), .clk(CLOCK), .Q(R1_q), .clr(RESET));
  Register #(.width(64)) R2 (.D(demultiplexer_1_out2), .en(demultiplexer_2_out2), .clk(CLOCK), .Q(R2_q), .clr(RESET));
  Register #(.width(64)) R3 (.D(demultiplexer_1_out3), .en(demultiplexer_2_out3), .clk(CLOCK), .Q(R3_q), .clr(RESET));
  Register #(.width(64)) R4 (.D(demultiplexer_1_out4), .en(demultiplexer_2_out4), .clk(CLOCK), .Q(R4_q), .clr(RESET));
  Register #(.width(64)) R5 (.D(demultiplexer_1_out5), .en(demultiplexer_2_out5), .clk(CLOCK), .Q(R5_q), .clr(RESET));
  Register #(.width(64)) R6 (.D(demultiplexer_1_out6), .en(demultiplexer_2_out6), .clk(CLOCK), .Q(R6_q), .clr(RESET));
  Register #(.width(64)) R7 (.D(demultiplexer_1_out7), .en(demultiplexer_2_out7), .clk(CLOCK), .Q(R7_q), .clr(RESET));
  Multiplexer #(.select(3), .width(64)) multiplexer_1 (
    .in0(R0_q), .in1(R1_q), .in2(R2_q), .in3(R3_q), .in4(R4_q), .in5(R5_q), .in6(R6_q), .in7(R7_q),
    .out(DATA_A_OUT), .sel(READ_A_SELECT));
  Multiplexer #(.select(3), .width(64)) multiplexer_2 (
    .in0(R0_q), .in1(R1_q), .in2(R2_q), .in3(R3_q), .in4(R4_q), .in5(R5_q), .in6(R6_q), .in7(R7_q),
    .out(DATA_B_OUT), .sel(READ_B_SELECT));
endmodule

module mch64 (
  input  CLOCK,
  input  RESET,
  input  [15:0] INSTRUCTION_DATA,
  input  [63:0] MEMORY_READ_DATA,
  output [7:0] INSTRUCTION_OUT,
  output [63:0] MEMORY_ADDRESS,
  output [63:0] MEMORY_WRITE_DATA,
  output MEMORY_WRITE,
  output TRUE
);

  wire controlunit_1_memory_to_reg, controlunit_1_mov_select, controlunit_1_reg_write;
  wire [1:0] controlunit_1_alu_op;
  wire [2:0] decode_1_ra, decode_1_rb, decode_1_rd;
  wire [3:0] decode_1_opcode;
  wire [8:0] decode_1_imm;
  wire [63:0] alu_1_result, bit_extender_1_out, multiplexer_1_out, multiplexer_2_out, regist_1_data_b_out;
  wire [63:8] pc_1_pc_out;

  PC pc_1 (.CLOCK(CLOCK), .RESET(RESET), .PC_OUT({pc_1_pc_out, INSTRUCTION_OUT}));  // open: DATA_IN, LOAD
  Decode decode_1 (
    .INSTRUCTION(INSTRUCTION_DATA), .OPCODE(decode_1_opcode), .RD(decode_1_rd), .RA(decode_1_ra),
    .RB(decode_1_rb), .IMM(decode_1_imm));
  assign bit_extender_1_out = {{55{1'b0}}, decode_1_imm};  // Bit_Extender bit_extender_1
  ControlUnit controlunit_1 (
    .OPCODE(decode_1_opcode), .REG_WRITE(controlunit_1_reg_write), .ALU_OP(controlunit_1_alu_op),
    .MOV_SELECT(controlunit_1_mov_select), .MEMORY_TO_REG(controlunit_1_memory_to_reg),
    .MEMORY_WRITE(MEMORY_WRITE));
  regist regist_1 (
    .DATA_IN(multiplexer_2_out), .READ_A_SELECT(decode_1_ra), .READ_B_SELECT(decode_1_rb),
    .WRITE_SELECT(decode_1_rd), .WRITE(controlunit_1_reg_write), .CLOCK(CLOCK), .RESET(RESET),
    .DATA_A_OUT(MEMORY_WRITE_DATA), .DATA_B_OUT(regist_1_data_b_out));
  ALU alu_1 (
    .IN0(MEMORY_WRITE_DATA), .IN1(regist_1_data_b_out), .MODE(controlunit_1_alu_op), .RESULT(alu_1_result));  // open: ZERO, NEGATIVE, CARRY
  Multiplexer #(.width(64)) multiplexer_1 (
    .in0(alu_1_result), .in1(bit_extender_1_out), .out(multiplexer_1_out), .sel(controlunit_1_mov_select));
  Multiplexer #(.width(64)) multiplexer_2 (
    .in0(multiplexer_1_out), .in1(MEMORY_READ_DATA), .out(multiplexer_2_out),
    .sel(controlunit_1_memory_to_reg));
  Multiplexer #(.width(64)) multiplexer_3 (
    .in0(MEMORY_WRITE_DATA), .in1(regist_1_data_b_out), .out(MEMORY_ADDRESS), .sel(MEMORY_WRITE));

  assign TRUE = 1'b1;
endmodule

module PC (
  input  [63:0] DATA_IN,
  input  LOAD,
  input  CLOCK,
  input  RESET,
  output [63:0] PC_OUT
);

  wire [63:0] adder_1_out, multiplexer_1_out;

  Register #(.width(64)) register_1 (.D(multiplexer_1_out), .clk(CLOCK), .Q(PC_OUT), .clr(RESET));  // open: en
  Adder #(.width(64)) adder_1 (.a(PC_OUT), .b(64'h1), .out(adder_1_out));  // open: cin, cout
  Multiplexer #(.width(64)) multiplexer_1 (.in0(adder_1_out), .in1(DATA_IN), .out(multiplexer_1_out), .sel(LOAD));
endmodule

module Decode (
  input  [15:0] INSTRUCTION,
  output [3:0] OPCODE,
  output [2:0] RD,
  output [2:0] RA,
  output [2:0] RB,
  output [8:0] IMM
);


  assign IMM = INSTRUCTION[8:0];
  assign OPCODE = INSTRUCTION[15:12];
  assign RA = INSTRUCTION[8:6];
  assign RB = INSTRUCTION[5:3];
  assign RD = INSTRUCTION[11:9];
endmodule

module ControlUnit (
  input  [3:0] OPCODE,
  output REG_WRITE,
  output [1:0] ALU_OP,
  output MOV_SELECT,
  output MEMORY_TO_REG,
  output MEMORY_WRITE
);

  wire decoder_1_out1, decoder_1_out2, decoder_1_out3, decoder_1_out4;

  Decoder #(.select(4)) decoder_1 (
    .out1(decoder_1_out1), .out2(decoder_1_out2), .out3(decoder_1_out3), .out4(decoder_1_out4),
    .out5(MOV_SELECT), .out6(MEMORY_TO_REG), .out7(MEMORY_WRITE), .sel(OPCODE));  // open: out0, out8, out9, out10, out11, out12, out13, out14, out15, en
  or or_1 (REG_WRITE, decoder_1_out1, decoder_1_out2, decoder_1_out3, decoder_1_out4, MOV_SELECT, MEMORY_TO_REG);
  or or_2 (ALU_OP[0], decoder_1_out2, decoder_1_out4);
  or or_3 (ALU_OP[1], decoder_1_out3, decoder_1_out4);
endmodule
